// Logisim project 1ort_praktikum.circ as structural Verilog: 5 circuits, main circuit 2_logkolo
module _2_logkolo (
  input  in_1,
  input  in_2,
  input  in_3,
  input  in_4,
  output out_5
);

  wire n1_built_logkolo_1_p3, n1_built_logkolo_2_p3;

  // _1_built_logkolo 1_built_logkolo_1: pin names not known; wires that end beside it: in_1, in_2, n1_built_logkolo_1_p3
  // _1_built_logkolo 1_built_logkolo_2: pin names not known; wires that end beside it: in_3, in_4, n1_built_logkolo_2_p3
  // _1_built_logkolo 1_built_logkolo_3: pin names not known; wires that end beside it: n1_built_logkolo_2_p3, n1_built_logkolo_1_p3, out_5
endmodule

module _1_logkolo (
  input  in_1,
  input  in_2,
  output out_3
);

  wire not_1_out, not_2_out, or_1_out, or_2_out;

  // Probe on not_1_out
  not not_1 (not_1_out, in_2);
  not not_2 (not_2_out, in_1);
  // Probe on not_2_out
  or or_1 (or_1_out, in_1, not_1_out);
  or or_2 (or_2_out, not_2_out, in_2);
  // Probe on or_1_out
  // Probe on or_2_out
  and and_1 (out_3, or_1_out, or_2_out);
endmodule

module _1_built_logkolo (
  input  a,
  input  b,
  output x
);

  wire not_1_out, not_2_out, or_1_out, or_2_out;

  not not_1 (not_1_out, b);
  not not_2 (not_2_out, a);
  or or_1 (or_1_out, a, not_1_out);
  or or_2 (or_2_out, not_2_out, b);
  and and_1 (x, or_1_out, or_2_out);
endmodule

module Dekoder (
  input  in_1,
  input  in_2,
  input  in_3,
  output out_4,
  output out_5,
  output out_6,
  output out_7,
  output out_8,
  output out_9,
  output out_10,
  output out_11
);

  Decoder #(.select(3)) decoder_1 (
    .out0(out_4), .out1(out_5), .out2(out_6), .out3(out_7), .out4(out_8), .out5(out_9), .out6(out_10),
    .out7(out_11), .sel({in_2, in_1, in_3}), .en(1'b1));
endmodule

module Dekoder_built (
  input  a,
  input  b,
  input  c,
  output x,
  output y,
  output z,
  output u,
  output v,
  output w,
  output s,
  output t
);

  wire and_1_out, and_2_out, and_3_out, and_4_out, and_5_out, and_6_out, and_7_out, and_8_out, not_1_out,
       not_2_out, not_3_out, not_4_out, not_5_out, not_6_out, not_7_out, not_8_out, not_9_out, not_10_out,
       not_11_out, not_12_out;

  not not_1 (not_1_out, a);
  not not_2 (not_2_out, b);
  not not_3 (not_3_out, a);
  not not_4 (not_4_out, b);
  not not_5 (not_5_out, b);
  not not_6 (not_6_out, b);
  not not_7 (not_7_out, a);
  not not_8 (not_8_out, a);
  and and_1 (and_1_out, a, b);
  not not_9 (not_9_out, c);
  and and_2 (and_2_out, a, b);
  and and_3 (and_3_out, not_1_out, not_2_out);
  not not_10 (not_10_out, c);
  and and_4 (and_4_out, not_3_out, not_4_out);
  and and_5 (and_5_out, a, not_5_out);
  not not_11 (not_11_out, c);
  and and_6 (and_6_out, a, not_6_out);
  and and_7 (and_7_out, not_7_out, b);
  not not_12 (not_12_out, c);
  and and_8 (and_8_out, not_8_out, b);
  and and_9 (s, and_1_out, not_9_out);
  and and_10 (t, and_2_out, c);
  and and_11 (x, and_3_out, not_10_out);
  and and_12 (y, and_4_out, c);
  and and_13 (z, and_5_out, not_11_out);
  and and_14 (u, and_6_out, c);
  and and_15 (v, and_7_out, not_12_out);
  and and_16 (w, and_8_out, c);
endmodule
